# Fritzing sketch CPEN291Lab1 (saved by Fritzing 0.9.4)
breadboards: 1

parts:
  Part1 = Adafruit T-Cobbler Plus [part_number="Adafruit #1989 and #2028"]
  LED3 = smd LED [color="Red (660nm)" package="0805 [SMD]"]
  LED4 = smd LED [color="Green (560nm)" package="0805 [SMD]"]
  LED5 = smd LED [color="Yellow (592nm)" package="0805 [SMD]"]
  R1 = Resistor [tolerance=±5% resistance=330 package="2010 [SMD]"]
  R2 = Resistor [tolerance=±0.05% resistance=220 package="2010 [SMD]"]
  R3 = Resistor [tolerance=±5% resistance=330 package="2010 [SMD]"]
  R4 = Resistor [tolerance=±5% resistance=10k package="2010 [SMD]"]
  SW1 = DIP SWITCH [package=dipswitch-02]

nets:
  N1: Part1.GND, R1.Pin_0, R2.Pin_0, R3.Pin_0, R4.Pin_1
  N2: Part1.GPIO13, SW1.2
  N3: Part1.GPIO19, SW1.1
  N4: Part1.GPIO16, LED3.anode
  N5: Part1.GPIO20, LED4.anode
  N6: Part1.GPIO21, LED5.anode
  N7: LED3.cathode, R2.Pin_1
  N8: LED4.cathode, R3.Pin_1
  N9: LED5.cathode, R1.Pin_1
  N10: R4.Pin_0, SW1.3, SW1.4

custom parts:
  Adafruit T-Cobbler Plus: The Raspberry Pi has landed on the Maker World like a 40-GPIO pinned, quad-USB ported, credit card sized bomb of DIY joy. And while you can use most of our great Model B accessories by hooking up our downgrade cable, its probably a good time to upgrade your set up and accessorize using all of the 40 pins. That's why we now carry the Assembled Adafruit Pi T-Cobbler Plus - Breakout + Cable for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
